// Logisim project Suh_FinalProject.circ as structural Verilog: 1 circuit, main circuit main
module main (
  input  X
);

  wire A_q, and_1_out, and_2_out, and_3_out, and_4_out, and_5_out, and_6_out, and_7_out, B_q, clock_1_out,
       counter_1_carry, d_ff_1_q, d_ff_1_qn, not_1_out, not_2_out, not_3_out, or_1_out, or_2_out, or_3_out,
       xor_1_out;

  not not_1 (not_1_out, B_q);
  not not_2 (not_2_out, A_q);
  not not_3 (not_3_out, counter_1_carry);
  and and_1 (and_1_out, A_q, not_1_out);
  or or_1 (or_1_out, A_q, B_q);
  and and_2 (and_2_out, counter_1_carry, not_2_out, B_q);
  and and_3 (and_3_out, not_3_out, A_q);
  and and_4 (and_4_out, A_q, not_1_out);
  and and_5 (and_5_out, not_2_out, not_1_out, X);
  and and_6 (and_6_out, B_q, not_3_out);
  and and_7 (and_7_out, A_q, not_1_out, counter_1_carry);
  Counter #(.max('hf)) counter_1 (
    .count(or_1_out), .carry(counter_1_carry), .clk(clock_1_out));  // open: load, D, Q, clr
  Clock clock_1 (.out(clock_1_out));
  or or_2 (or_2_out, and_2_out, and_3_out, and_4_out);
  or or_3 (or_3_out, and_5_out, and_6_out, and_7_out);
  xor xor_1 (xor_1_out, and_1_out, d_ff_1_q);
  D_Flip_Flop A (.clk(clock_1_out), .D(or_2_out), .Q(A_q));  // open: Qn, preset, en, reset
  D_Flip_Flop B (.clk(clock_1_out), .D(or_3_out), .Q(B_q));  // open: Qn, preset, en, reset
  D_Flip_Flop d_ff_1 (.clk(counter_1_carry), .D(xor_1_out), .Q(d_ff_1_q), .Qn(d_ff_1_qn));  // open: preset, en, reset
  LED led_1 (.in(B_q));
  LED led_2 (.in(and_1_out));
  _7_Segment_Display u_7_segment_display_1 (
    .f(d_ff_1_qn), .a(d_ff_1_qn), .b(1'b1), .e(d_ff_1_qn), .d(d_ff_1_qn), .c(1'b1));  // open: g, dp

  // Notes on the sheet:
  //   B+
  //   A+
  //   TC
  //   D flip flop configured as a T flip flop
  //   Door
  //   Moving
  //   Floor
endmodule
