// Logisim project lab8_2.circ as structural Verilog: 1 circuit, main circuit main
module main (
  input  in_1,
  output Door,
  output Floor,
  output Moving
);

  wire _2_2_out, _2_3_out, _2_out, _3_2_out, _3_3_out, _3_4_out, _3_out, clock_1_out, counter_1_carry,
       not_1_out, not_2_out, not_3_out, not_4_out, or_1_out, or_2_out, S0_q;

  not not_1 (not_1_out, S0_q);
  not not_2 (not_2_out, in_1);
  not not_3 (not_3_out, counter_1_carry);
  not not_4 (not_4_out, Door);
  and _2 (_2_out, not_3_out, S0_q);
  and _2_2 (_2_2_out, S0_q, not_4_out);
  and _3 (_3_out, counter_1_carry, not_1_out, Door);
  and _2_3 (_2_3_out, not_3_out, Door);
  and _3_2 (_3_2_out, in_1, not_1_out, not_4_out);
  and _3_3 (_3_3_out, counter_1_carry, S0_q, not_4_out);
  and _3_4 (_3_4_out, not_4_out, S0_q, counter_1_carry);
  and _2_4 (Moving, S0_q, not_4_out);
  or or_1 (or_1_out, _2_out, _2_2_out, _3_out);
  or or_2 (or_2_out, _2_3_out, _3_2_out, _3_3_out);
  Clock clock_1 (.out(clock_1_out));
  Counter #(.width(4), .max('hf)) counter_1 (
    .carry(counter_1_carry), .clk(clock_1_out));  // open: load, D, count, Q, clr
  D_Flip_Flop S0 (.clk(clock_1_out), .D(or_1_out), .Q(S0_q));  // open: Qn, preset, en, reset
  D_Flip_Flop S1 (.clk(clock_1_out), .D(or_2_out), .Q(Door));  // open: Qn, preset, en, reset
  T_Flip_Flop t_ff_1 (.clk(clock_1_out), .T(_3_4_out), .Q(Floor));  // open: Qn, preset, reset, en
endmodule
